# Fritzing sketch buttons-leds (saved by Fritzing 0.9.2b)
breadboards: 1

parts:
  Raspberry_Pi1 = Raspberry Pi 2
  R1 = Resistor [tolerance=±5% resistance=10k package=THT]
  S1 = Pushbutton [package="[THT]"]
  LED1 = LED - 5mm [color="Blue (470nm)" package="5 mm [THT]"]  # not connected
  R2 = Resistor [tolerance=±5% resistance=10k package=THT]
  S2 = Pushbutton [package="[THT]"]
  LED2 = LED - 5mm [color="Yellow (595nm)" package="5 mm [THT]"]  # not connected

nets:
  N1: Raspberry_Pi1.3v3, S1.Pin_1, S1.Pin_2, S2.Pin_1, S2.Pin_2
  N2: Raspberry_Pi1.GPIO4, R1.Pin_1, S1.Pin_3, S1.Pin_4
  N3: Raspberry_Pi1.GPIO23, R2.Pin_1, S2.Pin_3, S2.Pin_4
  N4: Raspberry_Pi1.GND, R1.Pin_0, R2.Pin_0
